# Fritzing sketch attiny85 (saved by Fritzing 0.8.3b)
circuit board: 3.30921cm x 2.27561cm
breadboards: 1

parts:
  ATTINY25/45/85 = ATtiny25/45/85 [package="8P3, 8-lead, 0.300\" Wide Body, PDIP"]
  R1 = Resistor [tolerance=±5% resistance=4.7k package=THT]
  IC1 = IC, SIP package, 3 pins [chip_label=RFe]
  RESET = Pushbutton [package="[THT]"]
  J6 = male pin header, 3 pins [form="♂ (male)" part_number=Onewire]
  J2 = male pin header, 3 pins [form="♂ (male)"]
  Q2 = NPN-Transistor [package="TO92 [THT]"]
  J9 = male pin header, 3 pins [form="♂ (male)"]
  R2 = Resistor [tolerance=±5% resistance=10k package=THT]
  Q1 = NPN-Transistor [package="TO92 [THT]"]
  DS1 = DS18B20 1-Wire Temperature Sensor [part_number=DS18B20]
  J10 = male pin header, 2 pins [form="♂ (male)"]

nets:
  N1: ATTINY25/45/85.(PCINT5/!RESET/ADC0/dW)_PB5, RESET.Pin_3, RESET.Pin_4, R2.Pin_0
  Port3: ATTINY25/45/85.(PCINT3/XTAL1/CLKI/!OC1B/ADC3)_PB3, J9.pin2
  Probe: ATTINY25/45/85.(PCINT4/XTAL2/CLKO/OC1B/ADC2)_PB4, Q2.C, Q1.E
  GND: ATTINY25/45/85.GND, IC1.pin3, RESET.Pin_1, RESET.Pin_2, J6.pin1, J2.pin3, Q2.E, Q2.B, J9.pin3, Q1.B, DS1.GND, J10.pin1
  Transmiter: ATTINY25/45/85.PB0_(MOSI/DI/SDA/AIN0/OC0A/!OC1A/AREF/PCINT0), IC1.pin1
  Onewire: ATTINY25/45/85.PB1_(MISO/DO/AIN1/OC0B/OC1A/PCINT1), R1.Pin_1, J6.pin2, DS1.DQ
  Port2: ATTINY25/45/85.PB2_(SCK/USCK/SCL/ADC1/TO/INT0/PCINT2), J2.pin2
  4.8V: ATTINY25/45/85.VCC, R1.Pin_0, IC1.pin2, J6.pin3, J2.pin1, J9.pin1, R2.Pin_1, Q1.C, DS1.VDD, J10.pin2

notes:
  5v
  GND
  Arduino-RFS, Wireless probe, 0.1
  Xavier Berger
  RF 433MHz
  (C) 2013
  R1
  R2

custom parts:
  ATtiny25/45/85: ATtiny25/45/85 8-bit AVR Microcontroller
